// Logisim project 2.circ as structural Verilog: 1 circuit, main circuit main
module main (
  input  A,
  input  B,
  input  C,
  input  A_2,
  input  B_2,
  input  C_2,
  output out_7,
  output out_8
);

  wire and_1_out, or_1_out;

  and and_1 (and_1_out, A, B);
  or or_1 (or_1_out, A_2, B_2);
  and and_2 (out_7, and_1_out, C);
  or or_2 (out_8, or_1_out, C_2);

  // Notes on the sheet:
  //   Antor Pritom Mondol
  //   2221077642
endmodule
